// Logisim project TheHackComputer.circ as structural Verilog
module Half_Adder (
  input  a,
  input  b,
  output Sum,
  output Carry
);

  xor xor_1 (Sum, a, b);
  and and_1 (Carry, a, b);
endmodule

module Full_Adder (
  input  carry_in,
  input  a,
  input  b,
  output sum,
  output carry_out
);

  wire half_adder_1_carry, half_adder_1_sum, half_adder_2_carry;

  Half_Adder half_adder_1 (.a(a), .b(b), .Sum(half_adder_1_sum), .Carry(half_adder_1_carry));
  Half_Adder half_adder_2 (.a(carry_in), .b(half_adder_1_sum), .Sum(sum), .Carry(half_adder_2_carry));
  or or_1 (carry_out, half_adder_2_carry, half_adder_1_carry);
endmodule

module _16_bit_Adder (
  input  carry_in,
  input  [15:0] a,
  input  [15:0] b,
  output [15:0] \output ,
  output carry_out
);

  wire full_adder_1_carry_out, full_adder_2_carry_out, full_adder_3_carry_out, full_adder_4_carry_out,
       full_adder_5_carry_out, full_adder_6_carry_out, full_adder_7_carry_out, full_adder_8_carry_out,
       full_adder_9_carry_out, full_adder_10_carry_out, full_adder_11_carry_out, full_adder_12_carry_out,
       full_adder_13_carry_out, full_adder_14_carry_out, full_adder_15_carry_out;

  Full_Adder full_adder_1 (
    .a(a[0]), .b(b[0]), .sum(\output [0]), .carry_out(full_adder_1_carry_out), .carry_in(carry_in));
  Full_Adder full_adder_2 (
    .a(a[8]), .b(b[8]), .sum(\output [8]), .carry_out(full_adder_2_carry_out),
    .carry_in(full_adder_15_carry_out));
  Full_Adder full_adder_3 (
    .a(a[1]), .b(b[1]), .sum(\output [1]), .carry_out(full_adder_3_carry_out),
    .carry_in(full_adder_1_carry_out));
  Full_Adder full_adder_4 (
    .a(a[9]), .b(b[9]), .sum(\output [9]), .carry_out(full_adder_4_carry_out),
    .carry_in(full_adder_2_carry_out));
  Full_Adder full_adder_5 (
    .a(a[2]), .b(b[2]), .sum(\output [2]), .carry_out(full_adder_5_carry_out),
    .carry_in(full_adder_3_carry_out));
  Full_Adder full_adder_6 (
    .a(a[10]), .b(b[10]), .sum(\output [10]), .carry_out(full_adder_6_carry_out),
    .carry_in(full_adder_4_carry_out));
  Full_Adder full_adder_7 (
    .a(a[3]), .b(b[3]), .sum(\output [3]), .carry_out(full_adder_7_carry_out),
    .carry_in(full_adder_5_carry_out));
  Full_Adder full_adder_8 (
    .a(a[11]), .b(b[11]), .sum(\output [11]), .carry_out(full_adder_8_carry_out),
    .carry_in(full_adder_6_carry_out));
  Full_Adder full_adder_9 (
    .a(a[4]), .b(b[4]), .sum(\output [4]), .carry_out(full_adder_9_carry_out),
    .carry_in(full_adder_7_carry_out));
  Full_Adder full_adder_10 (
    .a(a[12]), .b(b[12]), .sum(\output [12]), .carry_out(full_adder_10_carry_out),
    .carry_in(full_adder_8_carry_out));
  Full_Adder full_adder_11 (
    .a(a[5]), .b(b[5]), .sum(\output [5]), .carry_out(full_adder_11_carry_out),
    .carry_in(full_adder_9_carry_out));
  Full_Adder full_adder_12 (
    .a(a[13]), .b(b[13]), .sum(\output [13]), .carry_out(full_adder_12_carry_out),
    .carry_in(full_adder_10_carry_out));
  Full_Adder full_adder_13 (
    .a(a[6]), .b(b[6]), .sum(\output [6]), .carry_out(full_adder_13_carry_out),
    .carry_in(full_adder_11_carry_out));
  Full_Adder full_adder_14 (
    .a(a[14]), .b(b[14]), .sum(\output [14]), .carry_out(full_adder_14_carry_out),
    .carry_in(full_adder_12_carry_out));
  Full_Adder full_adder_15 (
    .a(a[7]), .b(b[7]), .sum(\output [7]), .carry_out(full_adder_15_carry_out),
    .carry_in(full_adder_13_carry_out));
  Full_Adder full_adder_16 (
    .a(a[15]), .b(b[15]), .sum(\output [15]), .carry_out(carry_out), .carry_in(full_adder_14_carry_out));
endmodule

module _16_bit_Incrementer (
  input  [15:0] \input ,
  output [15:0] \output 
);

  _16_bit_Adder u_16_bit_adder_1 (.carry_in(1'b0), .a(\input ), .b(16'h1), .\output (\output ));  // open: carry_out
endmodule

module Hack_ALU (
  input  nx__when_1__x___nx,
  input  ny__when_1__y___ny,
  input  f__when_1__x___y__else_x___y,
  input  zx__when_1__x_is_0,
  input  zy__when_1__y_is_0,
  input  no__when_1__out___nout,
  input  [15:0] x,
  input  [15:0] y,
  output [15:0] out,
  output ng__1_when_out_is___0,
  output zr__1_when_out_is_0
);

  wire or_1_out;
  wire [15:0] and_1_out, multiplexer_1_out, multiplexer_2_out, multiplexer_3_out, multiplexer_4_out,
       multiplexer_5_out, n16_bit_adder_1_output, not_1_out, not_2_out, not_3_out;

  Multiplexer #(.width(16), .enable("false")) multiplexer_1 (
    .in0(x), .in1({16{1'b0}}), .out(multiplexer_1_out), .sel(zx__when_1__x_is_0));
  assign not_1_out = ~multiplexer_1_out;  // NOT_Gate not_1, 16 bits wide
  Multiplexer #(.width(16), .enable("false")) multiplexer_2 (
    .in0(multiplexer_1_out), .in1(not_1_out), .out(multiplexer_2_out), .sel(nx__when_1__x___nx));
  Multiplexer #(.width(16), .enable("false")) multiplexer_3 (
    .in0(y), .in1({16{1'b0}}), .out(multiplexer_3_out), .sel(zy__when_1__y_is_0));
  assign not_2_out = ~multiplexer_3_out;  // NOT_Gate not_2, 16 bits wide
  Multiplexer #(.width(16), .enable("false")) multiplexer_4 (
    .in0(multiplexer_3_out), .in1(not_2_out), .out(multiplexer_4_out), .sel(ny__when_1__y___ny));
  assign and_1_out = multiplexer_2_out & multiplexer_4_out;  // AND_Gate and_1, 16 bits wide
  _16_bit_Adder u_16_bit_adder_1 (
    .carry_in(1'b0), .a(multiplexer_2_out), .b(multiplexer_4_out), .\output (n16_bit_adder_1_output));  // open: carry_out
  Multiplexer #(.width(16), .enable("false")) multiplexer_5 (
    .in0(and_1_out), .in1(n16_bit_adder_1_output), .out(multiplexer_5_out), .sel(f__when_1__x___y__else_x___y));
  assign not_3_out = ~multiplexer_5_out;  // NOT_Gate not_3, 16 bits wide
  Multiplexer #(.width(16), .enable("false")) multiplexer_6 (
    .in0(multiplexer_5_out), .in1(not_3_out), .out({ng__1_when_out_is___0, out[14:0]}),
    .sel(no__when_1__out___nout));
  or or_1 (or_1_out, ng__1_when_out_is___0, out[14], out[13], out[12], out[11], out[10], out[9], out[8], out[7], out[6], out[5], out[4], out[3], out[2], out[1], out[0]);
  not not_4 (zr__1_when_out_is_0, or_1_out);

  assign out[15] = ng__1_when_out_is___0;
endmodule

module Computer_Counter (
  input  increment__when_1__increment_by_1,
  input  load__when_1__loads_from_data_input,
  input  [15:0] data__value_to_load_into_counter,
  input  clock__value_may_update_on_trigger,
  input  reset__when_1__output_is_0_asynchronously,
  output [15:0] \output 
);

  wire not_1_out;
  wire [15:0] multiplexer_1_out, multiplexer_2_out, n16_bit_incrementer_1_output;

  not not_1 (not_1_out, increment__when_1__increment_by_1);
  _16_bit_Incrementer u_16_bit_incrementer_1 (.\input (\output ), .\output (n16_bit_incrementer_1_output));
  Multiplexer #(.width(16), .enable("false")) multiplexer_1 (
    .in0(n16_bit_incrementer_1_output), .in1(\output ), .out(multiplexer_1_out), .sel(not_1_out));
  Multiplexer #(.width(16), .enable("false")) multiplexer_2 (
    .in0(multiplexer_1_out), .in1(data__value_to_load_into_counter), .out(multiplexer_2_out),
    .sel(load__when_1__loads_from_data_input));
  Register #(.width(16)) register_1 (
    .D(multiplexer_2_out), .Q(\output ), .clk(clock__value_may_update_on_trigger),
    .clr(reset__when_1__output_is_0_asynchronously));  // open: en
endmodule

module Hack_CPU (
  input  [15:0] inst__instruction_to_be_excecuted,
  input  [15:0] inM__data_input,
  input  clock__pc_and_registers_update_on_trigger,
  input  reset__when_1__output_is_0_asynchronously,
  output writeM__when_1__will_write_to_data_memory,
  output [15:0] outM__data_output,
  output [15:0] addressM__address_output,
  output [15:0] pc__address_of_the_next_instruction_to_be_exectued
);

  wire hack_alu_1_ng__1_when_out_is___0, hack_alu_1_zr__1_when_out_is_0, hack_branching_controller_1_output,
       n16_way_line_driver_1_out_25, n16_way_line_driver_1_out_26, n16_way_line_driver_1_out_27,
       n16_way_line_driver_1_out_28, n16_way_line_driver_1_out_29, n16_way_line_driver_1_out_30,
       n16_way_line_driver_1_out_31, n16_way_line_driver_1_out_32, n16_way_line_driver_1_out_33, not_1_out,
       not_2_out, or_1_out;
  wire [2:0] n16_way_line_driver_1_out_21;
  wire [15:0] D_register_q, multiplexer_1_out, multiplexer_2_out;

  _16_Way_Line_Driver u_16_way_line_driver_1 (
    .in_4(inst__instruction_to_be_excecuted[0]), .in_5(inst__instruction_to_be_excecuted[1]),
    .in_6(inst__instruction_to_be_excecuted[2]), .in_7(inst__instruction_to_be_excecuted[3]),
    .in_8(inst__instruction_to_be_excecuted[4]), .in_9(inst__instruction_to_be_excecuted[5]),
    .in_10(inst__instruction_to_be_excecuted[6]), .in_11(inst__instruction_to_be_excecuted[7]),
    .in_12(inst__instruction_to_be_excecuted[8]), .in_13(inst__instruction_to_be_excecuted[9]),
    .in_14(inst__instruction_to_be_excecuted[10]), .in_15(inst__instruction_to_be_excecuted[11]),
    .in_16(inst__instruction_to_be_excecuted[12]), .enable(inst__instruction_to_be_excecuted[15]),
    .out_21(n16_way_line_driver_1_out_21[0]), .out_22(n16_way_line_driver_1_out_21[1]),
    .out_23(n16_way_line_driver_1_out_21[2]), .out_24(writeM__when_1__will_write_to_data_memory),
    .out_25(n16_way_line_driver_1_out_25), .out_26(n16_way_line_driver_1_out_26),
    .out_27(n16_way_line_driver_1_out_27), .out_28(n16_way_line_driver_1_out_28),
    .out_29(n16_way_line_driver_1_out_29), .out_30(n16_way_line_driver_1_out_30),
    .out_31(n16_way_line_driver_1_out_31), .out_32(n16_way_line_driver_1_out_32),
    .out_33(n16_way_line_driver_1_out_33));  // open: in_1, in_2, in_3, out_18, out_19, out_20
  Pull_Resistor pull_resistor_1 (.node(n16_way_line_driver_1_out_21[0]));
  Pull_Resistor pull_resistor_2 (.node(n16_way_line_driver_1_out_21[1]));
  Pull_Resistor pull_resistor_3 (.node(n16_way_line_driver_1_out_21[2]));
  Pull_Resistor pull_resistor_4 (.node(writeM__when_1__will_write_to_data_memory));
  Pull_Resistor pull_resistor_5 (.node(n16_way_line_driver_1_out_25));
  Pull_Resistor pull_resistor_6 (.node(n16_way_line_driver_1_out_26));
  Pull_Resistor pull_resistor_7 (.node(n16_way_line_driver_1_out_27));
  Pull_Resistor pull_resistor_8 (.node(n16_way_line_driver_1_out_28));
  Pull_Resistor pull_resistor_9 (.node(n16_way_line_driver_1_out_29));
  Pull_Resistor pull_resistor_10 (.node(n16_way_line_driver_1_out_30));
  Pull_Resistor pull_resistor_11 (.node(n16_way_line_driver_1_out_31));
  Pull_Resistor pull_resistor_12 (.node(n16_way_line_driver_1_out_32));
  Pull_Resistor pull_resistor_13 (.node(n16_way_line_driver_1_out_33));
  not not_1 (not_1_out, inst__instruction_to_be_excecuted[15]);
  or or_1 (or_1_out, not_1_out, n16_way_line_driver_1_out_26);
  Multiplexer #(.width(16), .enable("false")) multiplexer_1 (
    .in0(inst__instruction_to_be_excecuted), .in1(outM__data_output), .out(multiplexer_1_out),
    .sel(inst__instruction_to_be_excecuted[15]));
  Register #(.width(16)) A_register (
    .D(multiplexer_1_out), .en(or_1_out), .Q(addressM__address_output),
    .clk(clock__pc_and_registers_update_on_trigger), .clr(reset__when_1__output_is_0_asynchronously));
  Multiplexer #(.width(16), .enable("false")) multiplexer_2 (
    .in0(addressM__address_output), .in1(inM__data_input), .out(multiplexer_2_out),
    .sel(n16_way_line_driver_1_out_33));
  Register #(.width(16)) D_register (
    .D(outM__data_output), .en(n16_way_line_driver_1_out_25), .Q(D_register_q),
    .clk(clock__pc_and_registers_update_on_trigger), .clr(reset__when_1__output_is_0_asynchronously));
  Hack_Branching_Controller hack_branching_controller_1 (
    .zr(hack_alu_1_zr__1_when_out_is_0), .ng(hack_alu_1_ng__1_when_out_is___0),
    .\input (n16_way_line_driver_1_out_21), .\output (hack_branching_controller_1_output));
  not not_2 (not_2_out, hack_branching_controller_1_output);
  Hack_ALU hack_alu_1 (
    .x(D_register_q), .y(multiplexer_2_out), .out(outM__data_output),
    .zx__when_1__x_is_0(n16_way_line_driver_1_out_32), .nx__when_1__x___nx(n16_way_line_driver_1_out_31),
    .zy__when_1__y_is_0(n16_way_line_driver_1_out_30), .ny__when_1__y___ny(n16_way_line_driver_1_out_29),
    .f__when_1__x___y__else_x___y(n16_way_line_driver_1_out_28),
    .no__when_1__out___nout(n16_way_line_driver_1_out_27),
    .ng__1_when_out_is___0(hack_alu_1_ng__1_when_out_is___0),
    .zr__1_when_out_is_0(hack_alu_1_zr__1_when_out_is_0));
  Computer_Counter computer_counter_1 (
    .data__value_to_load_into_counter(addressM__address_output),
    .increment__when_1__increment_by_1(not_2_out),
    .load__when_1__loads_from_data_input(hack_branching_controller_1_output),
    .reset__when_1__output_is_0_asynchronously(reset__when_1__output_is_0_asynchronously),
    .clock__value_may_update_on_trigger(clock__pc_and_registers_update_on_trigger),
    .\output (pc__address_of_the_next_instruction_to_be_exectued));
endmodule

module Hack_Branching_Controller (
  input  zr,
  input  ng,
  input  [2:0] \input ,
  output \output 
);

  wire and_1_out, and_2_out, and_3_out, and_4_out, and_5_out, and_6_out, not_1_out, not_2_out;

  not not_1 (not_1_out, zr);
  not not_2 (not_2_out, ng);
  and and_1 (and_1_out, not_1_out, not_2_out);
  and and_2 (and_2_out, \input [0], and_1_out);
  and and_3 (and_3_out, not_2_out, zr);
  and and_4 (and_4_out, \input [1], and_3_out);
  or or_1 (\output , and_2_out, and_4_out, and_6_out);
  and and_5 (and_5_out, not_1_out, ng);
  and and_6 (and_6_out, \input [2], and_5_out);
endmodule

module _16_Way_Line_Driver (
  input  in_1,
  input  in_2,
  input  in_3,
  input  in_4,
  input  in_5,
  input  in_6,
  input  in_7,
  input  in_8,
  input  in_9,
  input  in_10,
  input  in_11,
  input  in_12,
  input  in_13,
  input  in_14,
  input  in_15,
  input  in_16,
  input  enable,
  output out_18,
  output out_19,
  output out_20,
  output out_21,
  output out_22,
  output out_23,
  output out_24,
  output out_25,
  output out_26,
  output out_27,
  output out_28,
  output out_29,
  output out_30,
  output out_31,
  output out_32,
  output out_33
);

  assign out_18 = enable ? in_1 : 1'bz;  // Controlled_Buffer controlled_buffer_1
  assign out_19 = enable ? in_2 : 1'bz;  // Controlled_Buffer controlled_buffer_2
  assign out_20 = enable ? in_3 : 1'bz;  // Controlled_Buffer controlled_buffer_3
  assign out_21 = enable ? in_4 : 1'bz;  // Controlled_Buffer controlled_buffer_4
  assign out_22 = enable ? in_5 : 1'bz;  // Controlled_Buffer controlled_buffer_5
  assign out_23 = enable ? in_6 : 1'bz;  // Controlled_Buffer controlled_buffer_6
  assign out_24 = enable ? in_7 : 1'bz;  // Controlled_Buffer controlled_buffer_7
  assign out_25 = enable ? in_8 : 1'bz;  // Controlled_Buffer controlled_buffer_8
  assign out_26 = enable ? in_9 : 1'bz;  // Controlled_Buffer controlled_buffer_9
  assign out_27 = enable ? in_10 : 1'bz;  // Controlled_Buffer controlled_buffer_10
  assign out_28 = enable ? in_11 : 1'bz;  // Controlled_Buffer controlled_buffer_11
  assign out_29 = enable ? in_12 : 1'bz;  // Controlled_Buffer controlled_buffer_12
  assign out_30 = enable ? in_13 : 1'bz;  // Controlled_Buffer controlled_buffer_13
  assign out_31 = enable ? in_14 : 1'bz;  // Controlled_Buffer controlled_buffer_14
  assign out_32 = enable ? in_15 : 1'bz;  // Controlled_Buffer controlled_buffer_15
  assign out_33 = enable ? in_16 : 1'bz;  // Controlled_Buffer controlled_buffer_16
endmodule

module Hack_Computer (
  input  Reset
);

  wire Clk_out, hack_cpu_1_writem__when_1__will_write_to_data_memory;
  wire [15:0] hack_cpu_1_addressm__address_output, hack_cpu_1_outm__data_output,
       hack_cpu_1_pc__address_of_the_next_instruction_to_be_exectued, ram_1_data, rom_1_data;

  ROM #(.addrWidth(16), .dataWidth(16)) rom_1 (
    .addr(hack_cpu_1_pc__address_of_the_next_instruction_to_be_exectued), .data(rom_1_data));  // open: sel
  Clock Clk (.out(Clk_out));
  Hack_CPU hack_cpu_1 (
    .inst__instruction_to_be_excecuted(rom_1_data), .inM__data_input(ram_1_data),
    .clock__pc_and_registers_update_on_trigger(Clk_out),
    .writeM__when_1__will_write_to_data_memory(hack_cpu_1_writem__when_1__will_write_to_data_memory),
    .outM__data_output(hack_cpu_1_outm__data_output),
    .addressM__address_output(hack_cpu_1_addressm__address_output),
    .pc__address_of_the_next_instruction_to_be_exectued(hack_cpu_1_pc__address_of_the_next_instruction_to_be_exectued),
    .reset__when_1__output_is_0_asynchronously(Reset));
  RAM #(.addrWidth(16), .dataWidth(16), .bus("separate")) ram_1 (
    .addr(hack_cpu_1_addressm__address_output), .din(hack_cpu_1_outm__data_output), .data(ram_1_data),
    .str(hack_cpu_1_writem__when_1__will_write_to_data_memory), .clk(Clk_out));  // open: sel, ld, clr

  // Notes on the sheet:
  //   contents of rom_1 (hex, n*v repeats v):
  //   1 fc10 10 e308 10 fc90 10 e304 0 fc10 2 f088 10 fc88 4 ea87 10 ea87
endmodule
